# Fritzing sketch RDM6300 (saved by Fritzing 0.9.3b)

parts:
  125_kHz_RFID_module1 = RDM6300
  Part1 = Arduino Nano (Rev3.0)

nets:
  N1: 125_kHz_RFID_module1.TX, Part1.D8
  GND: 125_kHz_RFID_module1.NULL, 125_kHz_RFID_module1.GND, Part1.GND
  +5V: 125_kHz_RFID_module1.+5V, Part1.5V

notes:
  RDM6300 reads EM4100 cards @125kHz. When a new card is detected, it is read and data sent via serial connection on the specified TX pin (Pin 8 shown here).
  Requires only three wires to Arduino:
  RDM6300 +5V <-> Arduino 5V
  RDM6300 GND <-> Arduino GND
  RDM6300 TX <-> Arduino Pin 8 (or other receive pin defined as Software Serial in code)
  RDM6300 ANT1 and ANT2 should be connected to the antenna (polarity is unimportant)
  The other pins on the RDM6300 board do not need to be connected... VCC and GND are duplicated, the middle pin of the block of five doesn't do anything, and the RX pin is also redundant, since the Arduino never sends data or commands *to* the RDM6300.

custom parts:
  RDM6300: 125 kHz RFID module (serial interface)
